// Logisim project DE0_CV_KEYPAD_FSM.circ as structural Verilog: 3 circuits, main circuit main
module main (
  input  EN,
  output [3:0] Y
);

  wire CLK_out, DECODE_1_hit, decoder_1_out0, decoder_1_out1, decoder_1_out2, decoder_1_out3, TWEQ_p5,
       TWEQ_p6, TWEQ_p7, TWEQ_p8;
  wire [1:0] DECODE_1_rowid, example_1_p6;

  Decoder #(.select(2), .enable("false")) decoder_1 (
    .out0(decoder_1_out0), .out1(decoder_1_out1), .out2(decoder_1_out2), .out3(decoder_1_out3),
    .sel(example_1_p6));
  // KeyPad TWEQ: pin names not known; wires that end beside it: decoder_1_out0, decoder_1_out1, decoder_1_out2, decoder_1_out3, TWEQ_p5, TWEQ_p6, TWEQ_p7, TWEQ_p8
  DECODE DECODE_1 (.L4(TWEQ_p8), .L2(TWEQ_p6), .L3(TWEQ_p7), .Hit(DECODE_1_hit), .L1(TWEQ_p5), .RowId(DECODE_1_rowid));
  Clock CLK (.out(CLK_out));
  // FSM_Entity #(.content("fsm example @[ 50 , 50 , 800 , 500 ] { in rowId [ 2 ] @[ 50 , 126 , 69 , 15 ] ;\nin active [ 1 ] @[ 50 , 171 , 43 , 15 ] ; out C [ 2 ] @[ 807 , 140 , 43 , 15 ]\n; out Hit [ 1 ] @[ 825 , 241 , 25 , 15 ] ; out key [ 4 ] @[ 794 , 447 , 56 , 15\n] ; codeWidth = 4 ; reset = S0 ; state S0 = \"0001\" @[ 500 , 183 , 30 , 30 ] {\ncommands @[ 545 , 197 , 50 , 40 ] { C = \"00\" ; Hit = active ; } transitions {\nS0 -> S2 when / active @[ 567 , 271 , 58 , 22 ] ; } } state S1 = \"1000\" @[ 273\n, 179 , 30 , 30 ] { commands @[ 318 , 194 , 40 , 40 ] { C = \"11\" ; Hit = active\n; } transitions { S1 -> S0 when / active @[ 407 , 136 , 58 , 22 ] ; } } state\nS2 = \"0010\" @[ 524 , 353 , 30 , 30 ] { commands @[ 569 , 367 , 60 , 40 ] { C =\n\"01\" ; Hit = active ; } transitions { S2 -> S3 when / active @[ 415 , 322 , 58\n, 22 ] ; } } state S3 = \"0100\" @[ 269 , 354 , 30 , 30 ] { commands @[ 314 , 368\n, 60 , 40 ] { C = \"10\" ; Hit = active ; } transitions { S3 -> S1 when / active\n@[ 284 , 263 , 58 , 22 ] ; } } }")) example_1: pin names not known; wires that end beside it: CLK_out, 1'b0, EN, DECODE_1_rowid, DECODE_1_hit, example_1_p6
  Register #(.width(4)) register_1 (
    .D({example_1_p6, DECODE_1_rowid}), .en(DECODE_1_hit), .clk(CLK_out), .Q(Y));  // open: clr
endmodule

module DECODE (
  input  L1,
  input  L2,
  input  L3,
  input  L4,
  output Hit,
  output [1:0] RowId
);

  wire not_1_out, not_2_out, not_3_out, not_4_out;

  not not_1 (not_1_out, L1);
  not not_2 (not_2_out, L2);
  not not_3 (not_3_out, L3);
  not not_4 (not_4_out, L4);
  or or_1 (Hit, L4, L3, L2, L1);
  or or_2 (RowId[1], L4, L3);
  or or_3 (RowId[0], L4, L2);
endmodule

module sdfg (
  input  in_1,
  output out_2
);

  buf buffer_1 (out_2, in_1);
endmodule
